// Logisim project procesor.circ as structural Verilog
module Procesor (
  input  [7:0] Adress,
  input  [7:0] in_2,
  input  LD,
  input  [7:0] in_4,
  input  [7:0] in_5,
  input  [2:0] in_6,
  input  in_7,
  input  [3:0] in_8,
  output [7:0] out_9,
  output [7:0] out_10,
  output [7:0] out_11,
  output out_12
);

  wire clock_1_out, clock_2_out;

  Clock clock_1 (.out(clock_1_out));
  RAM #(.bus("separate")) ram_1 (
    .addr(Adress), .din(in_2), .data(out_9), .clk(clock_1_out), .ld(LD));  // open: str, sel, clr
  ALU alu_1 (
    .R1__Value_of_first_register(in_4), .R2__Value_of_second_register(in_5), .OUT__ALU_output(out_10),
    .FL__output_to_FLAG(out_12), .COM__Value_of_command__0000_to_1111(in_8));
  Clock clock_2 (.out(clock_2_out));
  Registers registers_1 (.SET(out_10), .ADRESS(in_6), .out_5(out_11), .CLK(clock_2_out), .Control(in_7));
endmodule
